// Logisim project 2nd.circ as structural Verilog: 1 circuit, main circuit main
module main (
  input  A0,
  input  B0,
  input  A1,
  input  B1,
  input  A2,
  input  B2,
  input  A3,
  input  B3,
  output A_B,
  output A_B_2,
  output B_A
);

  wire and_1_out, and_2_out, and_3_out, and_4_out, and_5_out, and_6_out, and_7_out, and_8_out, and_9_out,
       and_10_out, and_11_out, and_12_out, and_13_out, and_14_out, and_15_out, and_16_out, and_17_out,
       and_18_out, not_1_out, not_2_out, not_3_out, not_4_out, not_5_out, not_6_out, not_7_out, not_8_out,
       not_9_out, not_10_out, not_11_out, not_12_out, not_13_out, not_14_out, not_15_out, not_16_out,
       not_17_out, not_18_out, not_19_out, not_20_out, not_21_out, not_22_out, xor_1_out, xor_2_out,
       xor_3_out, xor_4_out;

  not not_1 (not_1_out, A3);
  not not_2 (not_2_out, B3);
  and and_1 (and_1_out, A3, B3);
  and and_2 (and_2_out, not_1_out, not_2_out);
  xor xor_1 (xor_1_out, A0, B0);
  xor xor_2 (xor_2_out, A1, B1);
  xor xor_3 (xor_3_out, A2, B2);
  xor xor_4 (xor_4_out, A3, B3);
  not not_3 (not_3_out, A3);
  not not_4 (not_4_out, B3);
  not not_5 (not_5_out, xor_1_out);
  not not_6 (not_6_out, xor_2_out);
  not not_7 (not_7_out, xor_3_out);
  not not_8 (not_8_out, xor_4_out);
  and and_3 (and_3_out, not_3_out, not_4_out);
  and and_4 (and_4_out, A3, B3);
  not not_9 (not_9_out, A3);
  not not_10 (not_10_out, A2);
  not not_11 (not_11_out, A1);
  not not_12 (not_12_out, A0);
  and and_5 (and_5_out, not_9_out, B3);
  and and_6 (and_6_out, and_1_out, not_10_out, B2);
  and and_7 (and_7_out, not_11_out, B1, not_7_out, and_1_out);
  and and_8 (and_8_out, and_1_out, not_6_out, not_7_out, not_12_out, B0);
  not not_13 (not_13_out, B2);
  not not_14 (not_14_out, B1);
  not not_15 (not_15_out, B0);
  not not_16 (not_16_out, B3);
  not not_17 (not_17_out, B2);
  not not_18 (not_18_out, B1);
  not not_19 (not_19_out, B0);
  not not_20 (not_20_out, A2);
  and and_9 (and_9_out, not_20_out, B2, and_3_out);
  not not_21 (not_21_out, A1);
  and and_10 (and_10_out, not_21_out, B1, and_3_out, not_7_out);
  not not_22 (not_22_out, A0);
  and and_11 (and_11_out, not_22_out, B0, and_3_out, not_7_out, not_6_out);
  and and_12 (and_12_out, not_13_out, A2, and_4_out);
  and and_13 (and_13_out, not_14_out, A1, and_4_out, not_7_out);
  and and_14 (and_14_out, not_15_out, A0, and_4_out, not_7_out, not_6_out);
  and and_15 (and_15_out, A3, not_16_out);
  and and_16 (and_16_out, A2, not_17_out, and_2_out);
  and and_17 (and_17_out, and_2_out, not_7_out, A1, not_18_out);
  and and_18 (and_18_out, and_2_out, not_7_out, not_6_out, A0, not_19_out);
  or or_1 (A_B, and_5_out, and_6_out, and_7_out, and_8_out, and_16_out, and_17_out, and_18_out);
  and and_19 (A_B_2, not_5_out, not_6_out, not_7_out, not_8_out);
  or or_2 (B_A, and_9_out, and_10_out, and_11_out, and_12_out, and_13_out, and_14_out, and_15_out);
endmodule
