// Logisim project comparater.circ as structural Verilog: 1 circuit, main circuit main
module main (
  input  A0,
  input  B0,
  input  A1,
  input  B1,
  input  A2,
  input  B2,
  input  A3,
  input  B3,
  output out_9,
  output out_10,
  output out_11
);

  wire and_1_out, and_2_out, and_3_out, and_4_out, and_5_out, and_6_out, and_7_out, and_8_out, not_1_out,
       not_2_out, not_3_out, not_4_out, not_5_out, not_6_out, not_7_out, not_8_out, not_9_out, not_10_out,
       not_11_out, not_12_out, xor_1_out, xor_2_out, xor_3_out, xor_4_out;

  xor xor_1 (xor_1_out, A0, B0);
  xor xor_2 (xor_2_out, A1, B1);
  xor xor_3 (xor_3_out, A2, B2);
  xor xor_4 (xor_4_out, A3, B3);
  not not_1 (not_1_out, xor_1_out);
  not not_2 (not_2_out, xor_2_out);
  not not_3 (not_3_out, xor_3_out);
  not not_4 (not_4_out, xor_4_out);
  not not_5 (not_5_out, B3);
  not not_6 (not_6_out, B2);
  not not_7 (not_7_out, B1);
  not not_8 (not_8_out, B0);
  not not_9 (not_9_out, A3);
  not not_10 (not_10_out, A2);
  not not_11 (not_11_out, A1);
  not not_12 (not_12_out, A0);
  and and_1 (and_1_out, A3, not_5_out);
  and and_2 (and_2_out, A2, not_6_out, not_4_out);
  and and_3 (and_3_out, not_4_out, not_3_out, A1, not_7_out);
  and and_4 (and_4_out, not_4_out, not_3_out, not_2_out, A0, not_8_out);
  and and_5 (and_5_out, not_9_out, B3);
  and and_6 (and_6_out, not_10_out, B2, not_4_out);
  and and_7 (and_7_out, not_11_out, B1, not_4_out, not_3_out);
  and and_8 (and_8_out, not_12_out, B0, not_4_out, not_3_out, not_2_out);
  or or_1 (out_9, and_1_out, and_2_out, and_3_out, and_4_out);
  or or_2 (out_11, and_5_out, and_6_out, and_7_out, and_8_out);
  and and_9 (out_10, not_1_out, not_2_out, not_3_out, not_4_out);
endmodule
