// Logisim project first.circ as structural Verilog: 5 circuits, main circuit main
module main (
  input  A0,
  input  A1,
  input  A2,
  input  A3,
  input  B0,
  input  B1,
  input  B2,
  input  B3,
  output A_B,
  output A_B_2,
  output A_B_3
);

  intermediate_circuit intermediate_circuit_1 (
    .in_1(A0), .in_2(B0), .in_3(A1), .in_4(B1), .in_5(A2), .in_6(B2), .in_7(A3), .in_8(B3), .out_9(A_B),
    .out_10(A_B_2), .out_11(A_B_3));

  // Notes on the sheet:
  //                      Signed Comaparater
endmodule

module A_B (
  input  A0,
  input  B0,
  input  A1,
  input  B1,
  input  A2,
  input  B2,
  input  A3,
  input  B3,
  output A_B
);

  wire not_1_out, not_2_out, not_3_out, not_4_out, xor_1_out, xor_2_out, xor_3_out, xor_4_out;

  xor xor_1 (xor_1_out, A0, B0);
  xor xor_2 (xor_2_out, A1, B1);
  xor xor_3 (xor_3_out, A2, B2);
  xor xor_4 (xor_4_out, A3, B3);
  not not_1 (not_1_out, xor_1_out);
  not not_2 (not_2_out, xor_2_out);
  not not_3 (not_3_out, xor_3_out);
  not not_4 (not_4_out, xor_4_out);
  and and_1 (A_B, not_1_out, not_2_out, not_3_out, not_4_out);
endmodule

module A_B_2 (
  input  A0,
  input  B0,
  input  A1,
  input  B1,
  input  A2,
  input  B2,
  input  A3,
  input  B3,
  output A_B
);

  wire and_1_out, and_2_out, and_3_out, and_4_out, and_5_out, and_6_out, and_7_out, and_8_out, not_1_out,
       not_2_out, not_3_out, not_4_out, not_5_out, not_6_out, not_7_out, not_8_out, not_9_out, not_10_out,
       xor_1_out, xor_2_out;

  not not_1 (not_1_out, A3);
  not not_2 (not_2_out, B3);
  and and_1 (and_1_out, A3, B3);
  and and_2 (and_2_out, not_1_out, not_2_out);
  xor xor_1 (xor_1_out, A1, B1);
  xor xor_2 (xor_2_out, A2, B2);
  not not_3 (not_3_out, xor_1_out);
  not not_4 (not_4_out, xor_2_out);
  and and_3 (and_3_out, and_1_out, not_5_out, B2);
  not not_5 (not_5_out, A2);
  not not_6 (not_6_out, A1);
  and and_4 (and_4_out, not_6_out, B1, not_4_out, and_1_out);
  and and_5 (and_5_out, and_1_out, not_3_out, not_4_out, not_7_out, B0);
  not not_7 (not_7_out, A0);
  not not_8 (not_8_out, B2);
  not not_9 (not_9_out, B1);
  not not_10 (not_10_out, B0);
  and and_6 (and_6_out, A2, not_8_out, and_2_out);
  and and_7 (and_7_out, and_2_out, not_4_out, A1, not_9_out);
  and and_8 (and_8_out, and_2_out, not_4_out, not_3_out, A0, not_10_out);
  or or_1 (A_B, and_3_out, and_4_out, and_6_out, and_7_out, and_8_out);
endmodule

module A_B_2_2 (
  input  A0,
  input  B0,
  input  A1,
  input  B1,
  input  A2,
  input  B2,
  input  A3,
  input  B3,
  output B_A
);

  wire and_1_out, and_2_out, and_3_out, and_4_out, and_5_out, and_6_out, and_7_out, and_8_out, not_1_out,
       not_2_out, not_3_out, not_4_out, not_5_out, not_6_out, not_7_out, not_8_out, not_9_out, not_10_out,
       xor_1_out, xor_2_out;

  xor xor_1 (xor_1_out, A1, B1);
  not not_1 (not_1_out, xor_1_out);
  xor xor_2 (xor_2_out, A2, B2);
  not not_2 (not_2_out, xor_2_out);
  not not_3 (not_3_out, A3);
  not not_4 (not_4_out, B3);
  and and_1 (and_1_out, A3, B3);
  and and_2 (and_2_out, not_3_out, not_4_out);
  not not_5 (not_5_out, A2);
  not not_6 (not_6_out, A1);
  not not_7 (not_7_out, A0);
  not not_8 (not_8_out, B2);
  not not_9 (not_9_out, B1);
  not not_10 (not_10_out, B0);
  and and_3 (and_3_out, not_5_out, B2, and_2_out);
  and and_4 (and_4_out, not_6_out, B1, and_2_out, not_2_out);
  and and_5 (and_5_out, not_7_out, B0, and_2_out, not_2_out, not_1_out);
  and and_6 (and_6_out, not_8_out, A2, and_1_out);
  and and_7 (and_7_out, not_9_out, A1, and_1_out, not_2_out);
  and and_8 (and_8_out, not_10_out, A0, and_1_out, not_2_out, not_1_out);
  or or_1 (B_A, and_3_out, and_4_out, and_5_out, and_7_out, and_8_out);
endmodule

module intermediate_circuit (
  input  in_1,
  input  in_2,
  input  in_3,
  input  in_4,
  input  in_5,
  input  in_6,
  input  in_7,
  input  in_8,
  output out_9,
  output out_10,
  output out_11
);

  A_B A_B (.A0(in_1), .B0(in_2), .A1(in_3), .B1(in_4), .A2(in_5), .B2(in_6), .A3(in_7), .B3(in_8), .A_B(out_9));
  A_B_2 A_B_2 (.A0(in_1), .B0(in_2), .A1(in_3), .B1(in_4), .A2(in_5), .B2(in_6), .A3(in_7), .B3(in_8), .A_B(out_10));
  A_B_2_2 A_B_3 (.A0(in_1), .B0(in_2), .A1(in_3), .B1(in_4), .A2(in_5), .B2(in_6), .A3(in_7), .B3(in_8), .B_A(out_11));
endmodule
